# Fritzing sketch Wiring (saved by Fritzing 0.9.3b)
breadboards: 1

parts:
  Parts1 = SparkFun RedBoard [part_number=DEV-12757]
  U1 = LCD-16X2 [package=lcd-16x2]
  U2 = POT [package=trim_pot]
  Part1 = SparkFun_Vernier_Interface_Shield

nets:
  N1: Parts1.A0, Part1.AS1_AN2
  N2: Parts1.D11_PWM/MOSI, U1.E
  N3: Parts1.D12/MISO, U1.RS
  N4: Parts1.D2, U1.DB7
  N5: Parts1.D3_PWM, U1.DB6
  N6: Parts1.D4, U1.DB5
  N7: Parts1.D5_PWM, U1.DB4
  N8: Parts1.D6_PWM, Part1.D2_IO0
  5V: Parts1.5V, U1.VDD, U1.A, U2.A, Part1.5V
  GND: Parts1.GND, U1.VSS, U1.R_W, U1.K, U2.S, Part1.GND
  N9: U1.VO, U2.E

custom parts:
  SparkFun RedBoard: At SparkFun we use many Arduinos and we’re always looking for the simplest, most stable one. Each board is a bit different and no one board has everything we want, so we decided to make our own version that combines all our favorite features. The RedBoard combines the simplicity of the UNO’s Optiboot bootloader (which is used in the Pro series), the stability of the FTDI (which we all missed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
